# Fritzing sketch AMCB - Pcb (saved by Fritzing 0.9.3b)
circuit board: 6.71932cm x 5.41036cm
perfboards: 1

parts:
  StripA = screw terminal, 3 pins
  StripB = screw terminal, 3 pins
  R1 = Resistor [tolerance=±5% resistance=220 package=THT]
  R2 = Resistor [tolerance=±5% resistance=220 package=THT]
  Power_plug1 = Power plug  # not connected
  C3 = Capacitor Polarized [package=cpol-radial-1000uf-63v]  # not connected
  Composant2 = Adafruit Feather M0 WINC1500 [part_number="Adafruit #3010"]

nets:
  N1: StripA.pin1, StripB.pin1
  N2: StripA.pin2, R1.Pin_1
  N3: StripA.pin3, StripB.pin3
  N4: StripB.pin2, R2.Pin_0
  N5: R1.Pin_0, Composant2.D12
  N6: R2.Pin_1, Composant2.D11

notes:
  [écrivez votre texte ici]
  Rajouter 30 mm en longueur

custom parts:
  Adafruit Feather M0 WINC1500: This is the Adafruit Feather M0 WiFi w/ATWINC1500 - our take on an 'all-in-one' Arduino-compatible + high speed, reliable WiFi with built in USB and battery charging. Its an Adafruit Feather M0 with a WiFi module, ready to rock! Connect your Feather to the Internet with this fine new FCC-certified WiFi module from Atmel. This 802.11bgn-capable WiFi module is the best new thing for networking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
